// Logisim project Priority_Encoder-2.circ as structural Verilog: 1 circuit, main circuit main
module main (
  input  D0,
  input  D1,
  input  d2,
  input  d3,
  input  d4,
  input  d5,
  input  d6,
  input  d7,
  input  d8,
  input  d9,
  input  d10,
  input  d11,
  input  d12,
  input  d13,
  input  d14,
  input  D15,
  input  D16,
  input  D17,
  input  D18,
  input  D19,
  input  D20,
  input  D21,
  input  D22,
  input  D23,
  input  D24,
  input  D25,
  input  D26,
  input  D27,
  input  D28,
  input  D29,
  input  D30,
  input  D31,
  output Q0,
  output Q1,
  output Q2,
  output Q3,
  output Q4
);

  wire and_1_out, and_2_out, and_3_out, and_4_out, and_5_out, and_6_out, and_7_out, and_8_out, and_9_out,
       and_10_out, and_11_out, and_12_out, and_13_out, and_14_out, and_15_out, and_16_out, and_17_out,
       and_18_out, and_19_out, and_20_out, and_21_out, and_22_out, and_23_out, and_24_out, and_25_out,
       and_26_out, not_1_out, not_2_out, not_3_out, not_4_out, not_5_out, not_6_out, not_7_out, not_8_out,
       not_9_out, not_10_out, not_11_out, not_12_out, not_13_out, not_14_out, not_15_out, not_16_out,
       not_17_out, not_18_out, not_19_out, not_20_out, not_21_out, not_22_out, not_23_out, not_24_out,
       not_25_out, not_26_out, not_27_out, not_28_out, not_29_out, not_30_out, not_31_out, not_32_out,
       not_33_out, not_34_out, not_35_out, not_36_out, or_1_out, or_2_out, or_3_out, or_4_out, or_5_out,
       or_6_out, or_7_out, or_8_out, or_9_out, or_10_out, or_11_out, or_13_out;

  not not_1 (not_1_out, d9);
  or or_1 (or_1_out, d7, d6, and_2_out);
  not not_2 (not_2_out, not_12_out);
  not not_3 (not_3_out, d2);
  not not_4 (not_4_out, d11);
  not not_5 (not_5_out, d4);
  not not_6 (not_6_out, d6);
  not not_7 (not_7_out, d12);
  not not_8 (not_8_out, d14);
  and and_1 (and_1_out, not_1_out, not_11_out, or_1_out);
  or or_2 (or_2_out, d3, d2);
  and and_2 (and_2_out, or_2_out, not_5_out, not_9_out);
  not not_9 (not_9_out, d5);
  not not_10 (not_10_out, d9);
  not not_11 (not_11_out, d8);
  not not_12 (not_12_out, d10);
  or or_3 (or_3_out, and_1_out, d11, not_2_out);
  or or_4 (or_4_out, d8, d9, d10, d11, d12, d13, d14, D15);
  not not_13 (not_13_out, D17);
  not not_14 (not_14_out, D16);
  not not_15 (not_15_out, D18);
  not not_16 (not_16_out, D22);
  not not_17 (not_17_out, D19);
  not not_18 (not_18_out, D20);
  not not_19 (not_19_out, D23);
  not not_20 (not_20_out, D21);
  not not_21 (not_21_out, not_8_out);
  not not_22 (not_22_out, D17);
  not not_23 (not_23_out, D26);
  not not_24 (not_24_out, D24);
  and and_3 (and_3_out, or_4_out, not_14_out, not_13_out, not_15_out, not_17_out, not_18_out, not_20_out, not_16_out, not_19_out);
  not not_25 (not_25_out, d13);
  not not_26 (not_26_out, D28);
  and and_4 (and_4_out, D27, not_26_out);
  and and_5 (and_5_out, D25, not_23_out, not_26_out);
  and and_6 (and_6_out, D23, not_24_out, not_23_out, not_26_out);
  and and_7 (and_7_out, D21, not_16_out, not_24_out, not_23_out, not_26_out);
  and and_8 (and_8_out, D19, not_18_out, not_16_out, not_24_out, not_23_out, not_26_out);
  and and_9 (and_9_out, D17, not_15_out, not_18_out, not_16_out, not_24_out, not_23_out, not_26_out);
  and and_10 (and_10_out, D15, not_14_out, not_15_out, not_18_out, not_16_out, not_24_out, not_23_out, not_26_out);
  and and_11 (and_11_out, d13, not_8_out, not_14_out, not_15_out, not_18_out, not_16_out, not_24_out, not_23_out, not_26_out);
  and and_12 (and_12_out, d11, not_7_out, not_8_out, not_14_out, not_15_out, not_18_out, not_16_out, not_24_out, not_23_out, not_26_out);
  not not_27 (not_27_out, not_15_out);
  and and_13 (and_13_out, d9, not_12_out, not_7_out, not_8_out, not_14_out, not_15_out, not_18_out, not_16_out, not_24_out, not_23_out, not_26_out);
  and and_14 (and_14_out, d7, not_11_out, not_12_out, not_7_out, not_8_out, not_14_out, not_15_out, not_18_out, not_16_out, not_24_out, not_23_out, not_26_out);
  and and_15 (and_15_out, d5, not_6_out, not_11_out, not_12_out, not_7_out, not_8_out, not_14_out, not_15_out, not_18_out, not_16_out, not_24_out, not_23_out, not_26_out);
  and and_16 (and_16_out, d3, not_5_out, not_6_out, not_11_out, not_12_out, not_7_out, not_8_out, not_14_out, not_15_out, not_18_out, not_16_out, not_24_out, not_23_out, not_26_out);
  and and_17 (and_17_out, D1, not_3_out, not_5_out, not_6_out, not_11_out, not_12_out, not_7_out, not_8_out, not_14_out, not_15_out, not_18_out, not_16_out, not_24_out, not_23_out, not_26_out);
  or or_5 (or_5_out, d4, d5, d6, d7);
  not not_28 (not_28_out, D30);
  or or_6 (or_6_out, and_20_out, d12, d13, d14, D15);
  or or_7 (or_7_out, and_4_out, and_5_out, and_6_out, and_7_out, and_8_out, and_9_out, and_10_out, and_11_out, and_12_out, and_13_out, and_14_out, and_15_out, and_16_out, and_17_out, D29);
  and and_18 (and_18_out, or_7_out, not_28_out);
  and and_19 (and_19_out, or_3_out, not_7_out, not_25_out);
  and and_20 (and_20_out, not_4_out, or_5_out, not_10_out, not_11_out, not_12_out);
  and and_21 (and_21_out, or_6_out, not_14_out, not_13_out, not_15_out, not_17_out);
  not not_29 (not_29_out, D24);
  not not_30 (not_30_out, D25);
  not not_31 (not_31_out, D26);
  not not_32 (not_32_out, D27);
  or or_8 (or_8_out, and_19_out, not_21_out, D15);
  and and_22 (and_22_out, or_8_out, not_14_out, not_22_out);
  not not_33 (not_33_out, D21);
  or or_9 (or_9_out, and_22_out, not_27_out, D19);
  or or_10 (or_10_out, and_21_out, D20, D21, D22, D23);
  and and_23 (and_23_out, or_9_out, not_18_out, not_33_out);
  not not_34 (not_34_out, D25);
  and and_24 (and_24_out, or_10_out, not_29_out, not_30_out, not_31_out, not_32_out);
  or or_11 (or_11_out, and_23_out, D22, D23);
  and and_25 (and_25_out, or_11_out, not_24_out, not_34_out);
  not not_35 (not_35_out, D28);
  not not_36 (not_36_out, D29);
  or or_12 (Q0, and_18_out, D31);
  or or_13 (or_13_out, and_25_out, D26, D27);
  or or_14 (Q2, and_24_out, D28, D29, D30, D31);
  or or_15 (Q3, and_3_out, D24, D25, D26, D27, D28, D29, D30, D31);
  or or_16 (Q4, D16, D17, D18, D19, D20, D21, D22, D23, D24, D25, D26, D27, D28, D29, D30, D31);
  and and_26 (and_26_out, or_13_out, not_35_out, not_36_out);
  or or_17 (Q1, and_26_out, D30, D31);

  // Notes on the sheet:
  //   Name : Jay R Patel
  //   Roll No. : 19BCE085
  //   Topic : Priority Encoder
  //   Comprehensive Assignment
  //   32- 5 Bit Priority Encoder
endmodule
