// Logisim project Priority_Encoder.circ as structural Verilog: 1 circuit, main circuit main
module main (
  input  D3,
  input  D2,
  input  D1,
  input  D0,
  input  D0_2,
  input  D1_2,
  input  D2_2,
  input  D3_2,
  input  D4,
  input  D5,
  input  D6,
  input  D7,
  output B,
  output A,
  output V,
  output Q0,
  output Q1,
  output Q2
);

  wire and_1_out, and_2_out, and_3_out, and_4_out, and_5_out, and_6_out, not_1_out, not_2_out, not_3_out,
       not_4_out, not_5_out, or_2_out, or_5_out;

  not not_1 (not_1_out, D2);
  not not_2 (not_2_out, D2_2);
  not not_3 (not_3_out, D4);
  not not_4 (not_4_out, D5);
  and and_1 (and_1_out, not_1_out, D1);
  or or_1 (A, D3, D2);
  and and_2 (and_2_out, D1_2, not_2_out, not_3_out);
  and and_3 (and_3_out, D3_2, not_3_out);
  or or_2 (or_2_out, D2_2, D3_2);
  and and_4 (and_4_out, not_3_out, not_4_out);
  or or_3 (B, D3, and_1_out);
  or or_4 (V, A, D1, D0);
  or or_5 (or_5_out, and_2_out, and_3_out, D5);
  and and_5 (and_5_out, or_2_out, and_4_out);
  not not_5 (not_5_out, D6);
  and and_6 (and_6_out, or_5_out, not_5_out);
  or or_6 (Q0, and_6_out, D7);
  or or_7 (Q1, D6, D7, and_5_out);
  or or_8 (Q2, D6, D5, D4, D7);

  // Notes on the sheet:
  //   4-bit Priority Encoder
  //   8-bit Priority Encoder
  //   PRIORITY ENCODER
  //   Equations
  //   A = D3 + D2
  //   B = D3 + D2'.D1
  //   V = D3 + D2 + D1 + D0
  //   Equations
  //   Q2  = D4 + D5 + D6 +D7
  //   Q0 = D6 ( D4'.D2'.D1 + D4'.D3 + D5 ) + D7
  //   Q1 =  D5'.D4' ( D2 + D3 ) + D6 + D7
endmodule
